# Fritzing sketch Schema (saved by Fritzing 0.9.9b)
perfboards: 1

parts:
  JP4 = Header 10 [package=1x10-2mm-smd]  # not connected
  JP5 = Header 8 [package=1x08_smd]
  JP3 = Header 6 [package=1x06_smd_straight_alt]
  JP7 = Header 8 [package=1x08_smd]
  U1 = POT [package=pot_mammoth]
  J1 = JST-VHR-3N [part_number=JST-VHR-3N package=THT]
  J2 = JST-B3P-VH [part_number=JST-B3P-VH package=THT]
  S1 = Pushbutton [package="[THT]"]
  J3 = JST-B3P-VH [part_number=JST-B3P-VH package=THT]
  J4 = JST-VHR-3N [part_number=JST-VHR-3N package=THT]
  R1 = Resistor [tolerance=±5% power=0.25 resistance=10k package=THT]
  Parça1 = Arduino Leonardo (Rev3b)
  S2 = Pushbutton [package="[THT]"]
  J5 = JST-B3P-VH [part_number=JST-B3P-VH package=THT]
  J6 = JST-VHR-3N [part_number=JST-VHR-3N package=THT]
  R2 = Resistor [tolerance=±5% power=0.25 resistance=10k package=THT]

nets:
  N1: JP5.6, J3.pin3, R1.Pin_1
  N2: JP3.1, J2.pin2
  N3: JP7.5, J2.pin1
  N4: JP7.6, J2.pin3, R2.Pin_0
  N5: U1.S, J1.pin1
  N6: U1.A, J1.pin2
  N7: U1.E, J1.pin3
  N8: S1.Pin_3, S1.Pin_4, J4.pin1, J4.pin3, J4.pin_4, J4.pin_6
  N9: J3.pin1, J5.pin1
  N10: Parça1.D4/A6, J5.pin3, R2.Pin_1
  N11: S2.Pin_3, S2.Pin_4, J6.pin1, J6.pin3, J6.pin_4, J6.pin_6

notes:
  5v
  GND
  A0
  A1
  A2
  A3
  A4
  A5
  TX-1
  RX-0
  2
  ~3
  4
  ~5
  ~6
  7
  8
  ~9
  ~10
  ~11
  12
  ~13
  RETARDER
  SHIFTER TOGGLE1
  HANDBRAKE
